// Digital circuit Adder.dig as structural Verilog
module Adder (
  input  A0,
  input  B0,
  input  A1,
  input  B1,
  input  A2,
  input  B2,
  input  A3,
  input  B3,
  input  A4,
  input  B4,
  input  A5,
  input  B5,
  input  A6,
  input  B6,
  input  A7,
  input  B7,
  output S0,
  output S1,
  output S2,
  output S3,
  output S4,
  output S5,
  output S6,
  output S7,
  output Ov
);

  wire full_adder_2_cout, full_adder_3_cout, full_adder_4_cout, full_adder_5_cout, full_adder_6_cout,
       full_adder_7_cout, half_adder_1_cout;

  Full_Adder full_adder_1 (.A(A7), .B(B7), .Cin(full_adder_2_cout), .Sum(S7), .Cout(Ov));
  Full_Adder full_adder_2 (.A(A6), .B(B6), .Cin(full_adder_3_cout), .Sum(S6), .Cout(full_adder_2_cout));
  Full_Adder full_adder_3 (.A(A5), .B(B5), .Cin(full_adder_4_cout), .Sum(S5), .Cout(full_adder_3_cout));
  Full_Adder full_adder_4 (.A(A4), .B(B4), .Cin(full_adder_5_cout), .Sum(S4), .Cout(full_adder_4_cout));
  Full_Adder full_adder_5 (.A(A3), .B(B3), .Cin(full_adder_6_cout), .Sum(S3), .Cout(full_adder_5_cout));
  Full_Adder full_adder_6 (.A(A2), .B(B2), .Cin(full_adder_7_cout), .Sum(S2), .Cout(full_adder_6_cout));
  Full_Adder full_adder_7 (.A(A1), .B(B1), .Cin(half_adder_1_cout), .Sum(S1), .Cout(full_adder_7_cout));
  Half_Adder half_adder_1 (.A(A0), .B(B0), .Sum(S0), .Cout(half_adder_1_cout));
endmodule
