// Digital circuit Bit-Shifter.dig as structural Verilog
module Bit_Shifter (
  input  I0,
  input  Shift,
  input  I1,
  input  I2,
  input  I3,
  input  I4,
  input  I5,
  input  I6,
  input  I7,
  output S0,
  output S1,
  output S2,
  output S3,
  output S4,
  output S5,
  output S6,
  output S7
);

  wire and_1_out, and_2_out, and_3_out, and_4_out, and_5_out, and_6_out, and_7_out, and_8_out, and_9_out,
       and_10_out, and_11_out, and_12_out, and_13_out, and_14_out, and_15_out, and_16_out, not_1_out;

  and and_1 (and_1_out, Shift, I0);
  and and_2 (and_2_out, I0, not_1_out);
  and and_3 (and_3_out, Shift, I1);
  and and_4 (and_4_out, I1, not_1_out);
  and and_5 (and_5_out, Shift, I2);
  and and_6 (and_6_out, I2, not_1_out);
  and and_7 (and_7_out, Shift, I3);
  and and_8 (and_8_out, I3, not_1_out);
  and and_9 (and_9_out, Shift, I4);
  and and_10 (and_10_out, I4, not_1_out);
  and and_11 (and_11_out, Shift, I5);
  and and_12 (and_12_out, I5, not_1_out);
  and and_13 (and_13_out, Shift, I6);
  and and_14 (and_14_out, I6, not_1_out);
  and and_15 (and_15_out, Shift, I7);
  and and_16 (and_16_out, I7, not_1_out);
  not not_1 (not_1_out, Shift);
  or or_1 (S0, and_16_out, and_3_out);
  or or_2 (S1, and_2_out, and_5_out);
  or or_3 (S2, and_4_out, and_7_out);
  or or_4 (S3, and_6_out, and_9_out);
  or or_5 (S4, and_8_out, and_11_out);
  or or_6 (S5, and_10_out, and_13_out);
  or or_7 (S6, and_12_out, and_15_out);
  or or_8 (S7, and_14_out, and_1_out);
endmodule
