// Digital circuit Comparator.dig as structural Verilog
module Comparator (
  input  A0,
  input  B0,
  input  A1,
  input  A2,
  input  A3,
  input  A4,
  input  A5,
  input  A6,
  input  A7,
  input  B1,
  input  B2,
  input  B3,
  input  B4,
  input  B5,
  input  B6,
  input  B7,
  output A_lt_B,
  output A_eq_B,
  output A_gt_B
);

  wire full_comparator_1_eq, full_comparator_1_gt, full_comparator_1_lt, full_comparator_2_eq,
       full_comparator_2_gt, full_comparator_2_lt, full_comparator_3_eq, full_comparator_3_gt,
       full_comparator_3_lt, full_comparator_4_eq, full_comparator_4_gt, full_comparator_4_lt,
       full_comparator_5_eq, full_comparator_5_gt, full_comparator_5_lt, full_comparator_6_eq,
       full_comparator_6_gt, full_comparator_6_lt, half_comparator_1_eq, half_comparator_1_gt,
       half_comparator_1_lt;

  Half_Comparator half_comparator_1 (
    .A(A0), .B(B0), .lt(half_comparator_1_lt), .eq(half_comparator_1_eq), .gt(half_comparator_1_gt));
  Full_Comparator full_comparator_1 (
    .A(A1), .B(B1), .In_lt(half_comparator_1_lt), .In_eq(half_comparator_1_eq), .In_gt(half_comparator_1_gt),
    .lt(full_comparator_1_lt), .eq(full_comparator_1_eq), .gt(full_comparator_1_gt));
  Full_Comparator full_comparator_2 (
    .A(A2), .B(B2), .In_lt(full_comparator_1_lt), .In_eq(full_comparator_1_eq), .In_gt(full_comparator_1_gt),
    .lt(full_comparator_2_lt), .eq(full_comparator_2_eq), .gt(full_comparator_2_gt));
  Full_Comparator full_comparator_3 (
    .A(A3), .B(B3), .In_lt(full_comparator_2_lt), .In_eq(full_comparator_2_eq), .In_gt(full_comparator_2_gt),
    .lt(full_comparator_3_lt), .eq(full_comparator_3_eq), .gt(full_comparator_3_gt));
  Full_Comparator full_comparator_4 (
    .A(A4), .B(B4), .In_lt(full_comparator_3_lt), .In_eq(full_comparator_3_eq), .In_gt(full_comparator_3_gt),
    .lt(full_comparator_4_lt), .eq(full_comparator_4_eq), .gt(full_comparator_4_gt));
  Full_Comparator full_comparator_5 (
    .A(A5), .B(B5), .In_lt(full_comparator_4_lt), .In_eq(full_comparator_4_eq), .In_gt(full_comparator_4_gt),
    .lt(full_comparator_5_lt), .eq(full_comparator_5_eq), .gt(full_comparator_5_gt));
  Full_Comparator full_comparator_6 (
    .A(A6), .B(B6), .In_lt(full_comparator_5_lt), .In_eq(full_comparator_5_eq), .In_gt(full_comparator_5_gt),
    .lt(full_comparator_6_lt), .eq(full_comparator_6_eq), .gt(full_comparator_6_gt));
  Full_Comparator full_comparator_7 (
    .A(A7), .B(B7), .In_lt(full_comparator_6_lt), .In_eq(full_comparator_6_eq), .In_gt(full_comparator_6_gt),
    .lt(A_lt_B), .eq(A_eq_B), .gt(A_gt_B));
endmodule
