// Digital circuit Full-Comparator.dig as structural Verilog
module Full_Comparator (
  input  A,
  input  B,
  input  In_lt,
  input  In_eq,
  input  In_gt,
  output lt,
  output eq,
  output gt
);

  wire and_1_out, and_2_out, and_3_out, and_4_out, and_5_out, and_6_out, and_7_out, and_8_out, not_1_out,
       not_2_out;

  not not_1 (not_1_out, A);
  not not_2 (not_2_out, B);
  and and_1 (and_1_out, not_1_out, B);
  and and_2 (and_2_out, not_1_out, In_lt);
  and and_3 (and_3_out, B, In_lt);
  and and_4 (and_4_out, not_1_out, not_2_out, In_eq);
  and and_5 (and_5_out, A, B, In_eq);
  and and_6 (and_6_out, A, not_2_out);
  and and_7 (and_7_out, not_2_out, In_gt);
  and and_8 (and_8_out, A, In_gt);
  or or_1 (lt, and_1_out, and_2_out, and_3_out);
  or or_2 (eq, and_4_out, and_5_out);
  or or_3 (gt, and_6_out, and_7_out, and_8_out);
endmodule
