// Digital circuit Full-Subtractor.dig as structural Verilog
module Full_Subtractor (
  input  A,
  input  B,
  input  Cin,
  output Sub,
  output Cout
);

  wire and_1_out, and_2_out, xor_1_out;

  xor xor_1 (xor_1_out, A, B);
  and and_1 (and_1_out, Cin, ~xor_1_out);  // And
  and and_2 (and_2_out, ~A, B);  // And
  xor xor_2 (Sub, xor_1_out, Cin);
  or or_1 (Cout, and_1_out, and_2_out);
endmodule
