// Digital circuit Half-Comparator.dig as structural Verilog
module Half_Comparator (
  input  A,
  input  B,
  output lt,
  output eq,
  output gt
);

  wire not_1_out, not_2_out;

  not not_1 (not_1_out, A);
  not not_2 (not_2_out, B);
  and and_1 (lt, not_1_out, B);
  xnor xnor_1 (eq, A, B);
  and and_2 (gt, A, not_2_out);
endmodule
