// Digital circuit Half-Subtractor.dig as structural Verilog
module Half_Subtractor (
  input  A,
  input  B,
  output Sub,
  output Cout
);

  xor xor_1 (Sub, A, B);
  and and_1 (Cout, ~A, B);  // And
endmodule
