// Digital circuit Register.dig as structural Verilog
module Register (
  input  Clk,
  input  Read,
  input  D0,
  input  Write,
  input  Clr,
  input  D1,
  input  D2,
  input  D3,
  input  D4,
  input  D5,
  input  D6,
  input  D7,
  output Q0,
  output Q1,
  output Q2,
  output Q3,
  output Q4,
  output Q5,
  output Q6,
  output Q7
);

  wire and_1_out, and_2_out, and_3_out, and_4_out, and_5_out, and_6_out, and_7_out, and_8_out, and_9_out,
       d_ff_1_q, d_ff_2_q, d_ff_3_q, d_ff_4_q, d_ff_5_q, d_ff_6_q, d_ff_7_q, d_ff_8_q, diodeforward_1_out,
       diodeforward_2_out, diodeforward_3_out, diodeforward_4_out, diodeforward_5_out, diodeforward_6_out,
       diodeforward_7_out, diodeforward_8_out;

  and and_1 (and_1_out, Write, ~Clr);  // And
  and and_2 (and_2_out, D7, and_1_out);
  D_FF d_ff_1 (.D(and_2_out), .C(Clk), .Q(d_ff_1_q));  // open: nQ
  DiodeForward diodeforward_1 (.in(d_ff_1_q), .out(diodeforward_1_out));
  assign Q7 = Read ? diodeforward_1_out : 1'bz;  // Driver driver_1
  PullDown pulldown_1 (.out(diodeforward_1_out));
  and and_3 (and_3_out, D6, and_1_out);
  D_FF d_ff_2 (.D(and_3_out), .C(Clk), .Q(d_ff_2_q));  // open: nQ
  DiodeForward diodeforward_2 (.in(d_ff_2_q), .out(diodeforward_2_out));
  assign Q6 = Read ? diodeforward_2_out : 1'bz;  // Driver driver_2
  PullDown pulldown_2 (.out(diodeforward_2_out));
  and and_4 (and_4_out, D5, and_1_out);
  D_FF d_ff_3 (.D(and_4_out), .C(Clk), .Q(d_ff_3_q));  // open: nQ
  DiodeForward diodeforward_3 (.in(d_ff_3_q), .out(diodeforward_3_out));
  assign Q5 = Read ? diodeforward_3_out : 1'bz;  // Driver driver_3
  PullDown pulldown_3 (.out(diodeforward_3_out));
  and and_5 (and_5_out, D4, and_1_out);
  D_FF d_ff_4 (.D(and_5_out), .C(Clk), .Q(d_ff_4_q));  // open: nQ
  DiodeForward diodeforward_4 (.in(d_ff_4_q), .out(diodeforward_4_out));
  assign Q4 = Read ? diodeforward_4_out : 1'bz;  // Driver driver_4
  PullDown pulldown_4 (.out(diodeforward_4_out));
  and and_6 (and_6_out, D3, and_1_out);
  D_FF d_ff_5 (.D(and_6_out), .C(Clk), .Q(d_ff_5_q));  // open: nQ
  DiodeForward diodeforward_5 (.in(d_ff_5_q), .out(diodeforward_5_out));
  assign Q3 = Read ? diodeforward_5_out : 1'bz;  // Driver driver_5
  PullDown pulldown_5 (.out(diodeforward_5_out));
  and and_7 (and_7_out, D2, and_1_out);
  D_FF d_ff_6 (.D(and_7_out), .C(Clk), .Q(d_ff_6_q));  // open: nQ
  DiodeForward diodeforward_6 (.in(d_ff_6_q), .out(diodeforward_6_out));
  assign Q2 = Read ? diodeforward_6_out : 1'bz;  // Driver driver_6
  PullDown pulldown_6 (.out(diodeforward_6_out));
  and and_8 (and_8_out, D1, and_1_out);
  D_FF d_ff_7 (.D(and_8_out), .C(Clk), .Q(d_ff_7_q));  // open: nQ
  DiodeForward diodeforward_7 (.in(d_ff_7_q), .out(diodeforward_7_out));
  assign Q1 = Read ? diodeforward_7_out : 1'bz;  // Driver driver_7
  PullDown pulldown_7 (.out(diodeforward_7_out));
  and and_9 (and_9_out, D0, and_1_out);
  D_FF d_ff_8 (.D(and_9_out), .C(Clk), .Q(d_ff_8_q));  // open: nQ
  DiodeForward diodeforward_8 (.in(d_ff_8_q), .out(diodeforward_8_out));
  assign Q0 = Read ? diodeforward_8_out : 1'bz;  // Driver driver_8
  PullDown pulldown_8 (.out(diodeforward_8_out));
endmodule
