// Digital circuit Subtractor.dig as structural Verilog
module Subtractor (
  input  A0,
  input  B0,
  input  A1,
  input  B1,
  input  A2,
  input  B2,
  input  A3,
  input  B3,
  input  A4,
  input  B4,
  input  A5,
  input  B5,
  input  A6,
  input  B6,
  input  A7,
  input  B7,
  output S0,
  output S1,
  output S2,
  output S3,
  output S4,
  output S5,
  output S6,
  output S7,
  output Sig
);

  wire full_subtractor_2_cout, full_subtractor_3_cout, full_subtractor_4_cout, full_subtractor_5_cout,
       full_subtractor_6_cout, full_subtractor_7_cout, half_subtractor_1_cout;

  Full_Subtractor full_subtractor_1 (.A(A7), .B(B7), .Cin(full_subtractor_2_cout), .Sub(S7), .Cout(Sig));
  Full_Subtractor full_subtractor_2 (
    .A(A6), .B(B6), .Cin(full_subtractor_3_cout), .Sub(S6), .Cout(full_subtractor_2_cout));
  Full_Subtractor full_subtractor_3 (
    .A(A5), .B(B5), .Cin(full_subtractor_4_cout), .Sub(S5), .Cout(full_subtractor_3_cout));
  Full_Subtractor full_subtractor_4 (
    .A(A4), .B(B4), .Cin(full_subtractor_5_cout), .Sub(S4), .Cout(full_subtractor_4_cout));
  Full_Subtractor full_subtractor_5 (
    .A(A3), .B(B3), .Cin(full_subtractor_6_cout), .Sub(S3), .Cout(full_subtractor_5_cout));
  Full_Subtractor full_subtractor_6 (
    .A(A2), .B(B2), .Cin(full_subtractor_7_cout), .Sub(S2), .Cout(full_subtractor_6_cout));
  Full_Subtractor full_subtractor_7 (
    .A(A1), .B(B1), .Cin(half_subtractor_1_cout), .Sub(S1), .Cout(full_subtractor_7_cout));
  Half_Subtractor half_subtractor_1 (.A(A0), .B(B0), .Sub(S0), .Cout(half_subtractor_1_cout));
endmodule
